# Fritzing sketch Fredjes schema (saved by Fritzing 0.9.3b)

parts:
  J1 = Basic Servo
  WeMos_D1_Mini_Relay_Shield_V1 = WeMos D1 Mini Relay Shield V2
  J3 = Power Jack [package=power_jack_combo]
  M1 = RioRand LM2596
  J4 = Basic Servo
  M2 = DC Motor
  JP1 = FTDI_BASIC [package=ftdi_basic]

nets:
  GND: J1.gnd, WeMos_D1_Mini_Relay_Shield_V1.TX, M1.Pin_3, J4.gnd
  VCC: J1.vcc, WeMos_D1_Mini_Relay_Shield_V1.RX, M1.Pin_4, J4.vcc
  N1: J1.pulse, JP1.5
  N2: WeMos_D1_Mini_Relay_Shield_V1.D1, JP1.6
  N3: J3.GND, M1.Pin_2, JP1.3
  N4: J3.GNDBREAK, M1.Pin_1, M2.pin_2, JP1.2
  N5: J4.pulse, JP1.1

notes:
  MyRIO
  12V
  Pomp
